// Logisim project computadora_practica1.circ as structural Verilog: 1 circuit, main circuit main
module main (
  input  in_1,
  input  in_2,
  input  in_3
);

  wire A_out, and_1_out, clock_1_out, comparator_1_eq, decoder_1_out0, decoder_1_out1, decoder_1_out2,
       decoder_1_out3, decoder_1_out4, decoder_1_out5, decoder_1_out6, decoder_2_out1, decoder_2_out2,
       decoder_2_out3, decoder_2_out8, mar_2_out, mbr_2_out, multiplexer_2_out, or_1_out, pc_2_out, t3q0_out,
       t3q1_out, t3q2_out, t3q3_out, t4q0_out, t4q1_out, t4q2_out, t4q3_out, t5q0_out, t5q1_out, t5q3_out,
       t6q0_out, t6q1_out, t6q3_out, undriven, x1_out, x2_out, x3_out, x4_out;
  wire [2:0] bit_extender_1_out, Timer_q;
  wire [3:0] A_2_q, adder_1_out, adder_2_out, and_2_out, bitadder_1_out, divider_1_out, EXIT_q, IR_q, MAR_q,
       MBR_q, multiplexer_1_out, multiplexer_3_out, multiplexer_4_out, multiplexer_5_out, multiplexer_6_out,
       multiplier_1_out, nand_1_out, nor_1_out, odd_parity_1_out, odd_parity_2_out, or_2_out, PC_q,
       ram_1_data, ROP_q, shifter_1_out, shifter_2_out, shifter_3_out, subtractor_1_out, xnor_1_out,
       xor_1_out;

  Clock clock_1 (.out(clock_1_out));
  Multiplexer #(.width(4)) multiplexer_1 (
    .in0(adder_1_out), .in1(MBR_q), .out(multiplexer_1_out), .sel(t4q2_out));  // open: en
  assign bit_extender_1_out = {{2{1'b0}}, multiplexer_2_out};  // Bit_Extender bit_extender_1
  Multiplexer multiplexer_2 (.in0(clock_1_out), .in1(undriven), .out(multiplexer_2_out), .sel(and_1_out));  // open: en
  Register #(.width(4)) PC (.D(multiplexer_1_out), .en(pc_2_out), .Q(PC_q), .clk(multiplexer_2_out));  // open: clr
  or pc_2 (pc_2_out, x3_out, t4q2_out);
  Counter #(.width(3), .max('h7)) Timer (
    .D(bit_extender_1_out), .count(in_3), .Q(Timer_q), .clk(multiplexer_2_out));  // open: load, carry, clr
  Adder #(.width(4)) adder_1 (.a(4'b0001), .b(PC_q), .out(adder_1_out));  // open: cin, cout
  Multiplexer #(.width(4)) multiplexer_3 (.in0(PC_q), .in1(MBR_q), .out(multiplexer_3_out), .sel(x2_out));  // open: en
  Register #(.width(4)) MAR (.D(multiplexer_3_out), .en(mar_2_out), .Q(MAR_q), .clk(multiplexer_2_out));  // open: clr
  or mar_2 (mar_2_out, x1_out, x2_out);
  Decoder #(.select(3)) decoder_1 (
    .out0(decoder_1_out0), .out1(decoder_1_out1), .out2(decoder_1_out2), .out3(decoder_1_out3),
    .out4(decoder_1_out4), .out5(decoder_1_out5), .out6(decoder_1_out6), .sel(Timer_q));  // open: out7, en
  Decoder #(.select(4)) decoder_2 (
    .out1(decoder_2_out1), .out2(decoder_2_out2), .out3(decoder_2_out3), .out8(decoder_2_out8), .sel(IR_q));  // open: out0, out4, out5, out6, out7, out9, out10, out11, out12, out13, out14, out15, en
  or or_1 (or_1_out, mar_2_out, x4_out, t6q1_out);
  Comparator #(.width(4)) comparator_1 (.a(MAR_q), .b(MBR_q), .eq(comparator_1_eq));  // open: gt, lt
  and t6q0 (t6q0_out, decoder_1_out6, decoder_2_out1);
  and t6q1 (t6q1_out, decoder_1_out6, decoder_2_out2);
  // AND_Gate t6q2 has open pins: in0=decoder_1_out6, in1=decoder_2_out3, out=open
  and t6q3 (t6q3_out, decoder_1_out6, decoder_2_out8);
  and t5q0 (t5q0_out, decoder_1_out5, decoder_2_out1);
  and t5q1 (t5q1_out, decoder_1_out5, decoder_2_out2);
  // AND_Gate t5q2 has open pins: in0=decoder_1_out5, in1=decoder_2_out3, out=open
  and t5q3 (t5q3_out, decoder_1_out5, decoder_2_out8);
  and t4q0 (t4q0_out, decoder_1_out4, decoder_2_out1);
  and t4q1 (t4q1_out, decoder_1_out4, decoder_2_out2);
  and t4q2 (t4q2_out, decoder_1_out4, decoder_2_out3);
  and t4q3 (t4q3_out, decoder_1_out4, decoder_2_out8);
  and t3q0 (t3q0_out, decoder_1_out3, decoder_2_out1);
  and t3q1 (t3q1_out, decoder_1_out3, decoder_2_out2);
  and t3q2 (t3q2_out, decoder_1_out3, decoder_2_out3);
  and t3q3 (t3q3_out, decoder_1_out3, decoder_2_out8);
  // AND_Gate t2q0 has open pins: in0=decoder_1_out2, in1=decoder_2_out1, out=open
  // AND_Gate t2q1 has open pins: in0=decoder_1_out2, in1=decoder_2_out2, out=open
  // AND_Gate t2q2 has open pins: in0=decoder_1_out2, in1=decoder_2_out3, out=open
  // AND_Gate t2q3 has open pins: in0=decoder_1_out2, in1=decoder_2_out8, out=open
  // AND_Gate t1q0 has open pins: in0=decoder_1_out1, in1=decoder_2_out1, out=open
  // AND_Gate t1q1 has open pins: in0=decoder_1_out1, in1=decoder_2_out2, out=open
  // AND_Gate t1q2 has open pins: in0=decoder_1_out1, in1=decoder_2_out3, out=open
  // AND_Gate t1q3 has open pins: in0=decoder_1_out1, in1=decoder_2_out8, out=open
  // AND_Gate t0q0 has open pins: in0=decoder_1_out0, in1=decoder_2_out1, out=open
  // AND_Gate t0q1 has open pins: in0=decoder_1_out0, in1=decoder_2_out2, out=open
  // AND_Gate t0q2 has open pins: in0=decoder_1_out0, in1=decoder_2_out3, out=open
  // AND_Gate t0q3 has open pins: in0=decoder_1_out0, in1=decoder_2_out8, out=open
  and and_1 (and_1_out, comparator_1_eq, t4q2_out);
  RAM #(.addrWidth(4), .dataWidth(4), .bus("separate")) ram_1 (
    .addr(MAR_q), .din(MBR_q), .data(ram_1_data), .str(t6q1_out), .clk(or_1_out), .ld(x4_out));  // open: sel, clr
  or x1 (x1_out, decoder_1_out0, t4q3_out, decoder_1_out2);
  or x2 (x2_out, t4q0_out, t4q1_out);
  Multiplexer #(.width(4)) multiplexer_4 (
    .in0(A_2_q), .in1(ram_1_data), .out(multiplexer_4_out), .sel(x4_out));  // open: en
  or x3 (x3_out, decoder_1_out1, t5q3_out, t3q0_out, t3q1_out, t3q2_out, t3q3_out);
  or x4 (x4_out, decoder_1_out1, t5q0_out, t5q3_out, t3q0_out, t3q1_out, t3q2_out, t3q3_out);
  Register #(.width(4)) MBR (.D(multiplexer_4_out), .en(mbr_2_out), .Q(MBR_q), .clk(multiplexer_2_out));  // open: clr
  or mbr_2 (mbr_2_out, t5q1_out, x4_out);
  Register #(.width(4)) IR (.D(MBR_q), .en(decoder_1_out2), .Q(IR_q), .clk(multiplexer_2_out));  // open: clr
  Adder #(.width(4)) adder_2 (.a(MBR_q), .b(A_2_q), .out(adder_2_out));  // open: cin, cout
  Subtractor #(.width(4)) subtractor_1 (.a(MBR_q), .b(A_2_q), .out(subtractor_1_out));  // open: bin, bout
  Multiplier #(.width(4)) multiplier_1 (.a(MBR_q), .b(A_2_q), .out(multiplier_1_out));  // open: cin, cout
  Divider #(.width(4)) divider_1 (.a(MBR_q), .b(A_2_q), .out(divider_1_out));  // open: upper, rem
  assign odd_parity_1_out = MBR_q;  // Odd_Parity odd_parity_1, 4 bits wide Odd_Parity
  Shifter #(.width(4)) shifter_1 (.in(A_2_q), .\dist (2'b11), .out(shifter_1_out));
  Shifter #(.width(4)) shifter_2 (.in(A_2_q), .\dist (2'b01), .out(shifter_2_out));
  BitAdder #(.width(4)) bitadder_1 (.in0(MBR_q), .in1(A_2_q), .out(bitadder_1_out));
  assign and_2_out = MBR_q & A_2_q;  // AND_Gate and_2, 4 bits wide
  assign or_2_out = MBR_q | A_2_q;  // OR_Gate or_2, 4 bits wide
  assign nor_1_out = ~(MBR_q | A_2_q);  // NOR_Gate nor_1, 4 bits wide
  assign xor_1_out = MBR_q ^ A_2_q;  // XOR_Gate xor_1, 4 bits wide
  assign xnor_1_out = ~(MBR_q ^ A_2_q);  // XNOR_Gate xnor_1, 4 bits wide
  assign nand_1_out = ~(MBR_q & A_2_q);  // NAND_Gate nand_1, 4 bits wide
  Shifter #(.width(4)) shifter_3 (.in(A_2_q), .\dist (2'b10), .out(shifter_3_out));
  assign odd_parity_2_out = MBR_q ^ A_2_q;  // Odd_Parity odd_parity_2, 4 bits wide
  Multiplexer #(.width(4)) multiplexer_5 (
    .in0(MBR_q), .in1(multiplexer_6_out), .out(multiplexer_5_out), .sel(t6q3_out));  // open: en
  or A (A_out, t6q0_out, t6q3_out);
  Register #(.width(4)) ROP (.D(MBR_q), .en(t4q3_out), .Q(ROP_q), .clk(multiplexer_2_out));  // open: clr
  Register #(.width(4)) A_2 (.D(multiplexer_5_out), .en(A_out), .Q(A_2_q), .clk(multiplexer_2_out));  // open: clr
  Multiplexer #(.select(4), .width(4)) multiplexer_6 (
    .in0(adder_2_out), .in1(subtractor_1_out), .in2(multiplier_1_out), .in3(divider_1_out),
    .in4(odd_parity_1_out), .in5(shifter_1_out), .in6(shifter_2_out), .in7(bitadder_1_out), .in8(and_2_out),
    .in9(or_2_out), .in10(nor_1_out), .in11(xor_1_out), .in12(xnor_1_out), .in13(nand_1_out),
    .in14(shifter_3_out), .in15(odd_parity_2_out), .out(multiplexer_6_out), .sel(ROP_q));  // open: en
  Register #(.width(4)) EXIT (.D(A_2_q), .en(in_1), .Q(EXIT_q), .clk(multiplexer_2_out));  // open: clr
  Hex_Digit_Display hex_digit_display_1 (.value(EXIT_q));  // open: dp

  // Notes on the sheet:
  //   instrucciones
  //   tiempos
  //   x12,IR
  //   x6,A
  //   x8,M
  //   x7
  //   x5
  //   pc
  //   x9,ROP
  //   mar
  //   mar
  //   x10,A
  //   mbr
  //   pc
  //   mbr
endmodule
